# Fritzing sketch WindSensorMKR (saved by Fritzing 0.9.8b)
circuit board: 8.8cm x 4.6cm

parts:
  R1 = Resistor [tolerance=±1% resistance=10k power=0.25 package=THT]
  RJ11_MISOL = RJ11 Jack [package=rj11-6]
  R3 = Resistor [tolerance=±1% resistance=560k power=0.25 package=THT]
  R4 = Resistor [tolerance=±1% resistance=390k power=0.25 package=THT]
  TP4056 = TP4056 [chip_label=TP4056 package="DIP (Dual Inline) [THT]"]
  C2 = Film/Foil Capacitor [capacitance=100nF voltage=35V package="5mm [THT, pp]"]
  C1 = Film/Foil Capacitor [capacitance=100nF voltage=35V package="5mm [THT, pp]"]
  U1_ON-OFF = SPST Switch [package=switch-spdt_kit]
  D1 = Schottky Diode [part_number=1N5817 package="300 mil [THT]"]
  D2 = Schottky Diode [part_number=1N5817 package="300 mil [THT]"]
  +BAT- = Screw terminal - 2 pins [package=THT]
  D3 = Schottky Diode [part_number=1N5817 package="300 mil [THT]"]
  D4 = Schottky Diode [part_number=1N5817 package="300 mil [THT]"]
  R2 = Resistor [tolerance=±1% resistance=100k power=0.25 package=THT]
  +SOLAR- = Screw terminal - 2 pins [package=THT]
  MKRFOX1200 = Arduino MKR Fox 1200
  R5 = Resistor [tolerance=±1% resistance=1k power=0.25 package=THT]
  R6 = Resistor [tolerance=±1% resistance=1k power=0.25 package=THT]

nets:
  pinGirAdc: R1.Pin_0, C2.-, D2.cathode, D3.anode, MKRFOX1200.A6, R6.Pin_0
  pinGirAlim: R1.Pin_1, D3.cathode, MKRFOX1200.~5
  GND: RJ11_MISOL.2, RJ11_MISOL.3, R4.Pin_0, TP4056.pin2, TP4056.pin5, TP4056.pin6, C2.+, C1.+, D1.anode, D2.anode, +BAT-.pin2, +SOLAR-.pin2, MKRFOX1200.GND
  N1: RJ11_MISOL.4, R6.Pin_1
  N2: RJ11_MISOL.5, R5.Pin_1
  N3: R3.Pin_0, R4.Pin_1, MKRFOX1200.A4
  Vbat: R3.Pin_1, TP4056.pin4, +BAT-.pin1
  N4: TP4056.pin1, +SOLAR-.pin1
  N5: TP4056.pin3, U1_ON-OFF.P
  intPinAnemo: C1.-, D1.cathode, D4.anode, R2.Pin_1, MKRFOX1200.~4, R5.Pin_0
  N6: U1_ON-OFF.O, MKRFOX1200.VIN
  Vcc: D4.cathode, R2.Pin_0, MKRFOX1200.VCC

notes:
  yellow
  green
  red
  black
  WindSensorMKR1200

custom parts:
  TP4056: A DIP stand-in part for whatever IC you want. With 6 pins on a 300mil dual inline package (DIP) footprint.
